# Fritzing sketch ArduCAM_5MP_Schema (saved by Fritzing 0.9.4)

parts:
  Componente1 = Arduino Uno (Rev3)
  arducam1 = Arducam 5mp mini

nets:
  N1: Componente1.D10_PWM/SS, arducam1.MOSI
  N2: Componente1.D11_PWM/MOSI, arducam1.MISO
  N3: Componente1.D12/MISO, arducam1.SCK
  N4: Componente1.A4/SDA, arducam1.SDA
  N5: Componente1.A5/SCL, arducam1.SCL
  N6: Componente1.D7, arducam1.CS
  5V: Componente1.5V, arducam1.VCC
  GND: Componente1.GND, arducam1.GND

custom parts:
  Arducam 5mp mini: arducam mini is a 5mp camera with a i2c and spi interface
