# Fritzing sketch PN532_Shield_Schema (saved by Fritzing 0.9.4)

parts:
  Componente1 = Adafruit PN532 NFC RFID Controller Shield [part_number="Adafruit #789"]
  Componente2 = Arduino Uno (Rev3)

nets:
  +3.3V: Componente1.+3.3V, Componente2.3V3
  N1: Componente1.5.0V, Componente2.5V
  N2: Componente1.A0, Componente2.A0
  N3: Componente1.A1, Componente2.A1
  N4: Componente1.A2, Componente2.A2
  N5: Componente1.A3, Componente2.A3
  N6: Componente1.SDA, Componente2.A4/SDA
  N7: Componente1.SCL, Componente2.A5/SCL
  N8: Componente1.AREF, Componente2.AREF
  N9: Componente1.D0, Componente2.D0/RX
  N10: Componente1.D1, Componente2.D1/TX
  N11: Componente1.D2, Componente2.D2
  N12: Componente1.D3, Componente2.D3_PWM
  N13: Componente1.D4, Componente2.D4
  N14: Componente1.D5, Componente2.D5_PWM
  N15: Componente1.D6, Componente2.D6_PWM
  N16: Componente1.D7, Componente2.D7
  N17: Componente1.D8, Componente2.D8
  N18: Componente1.D9, Componente2.D9_PWM
  N19: Componente1.D10, Componente2.D10_PWM/SS
  N20: Componente1.D11, Componente2.D11_PWM/MOSI
  N21: Componente1.D12, Componente2.D12/MISO
  N22: Componente1.D13, Componente2.D13/SCK
  GND: Componente1.GND, Componente2.GND
  N23: Componente1.IOREF, Componente2.ioref
  N24: Componente1.NC, Componente2.N/C
  N25: Componente1.RST, Componente2.RESET
  VIN: Componente1.VIN, Componente2.VIN

custom parts:
  Adafruit PN532 NFC RFID Controller Shield: We've taken our popular Adafruit PN532 breakout board and turned it into a shield - the perfect tool for any 13.56MHz RFID or NFC application. The Adafruit NFC shield uses the PN532 chip-set (the most popular NFC chip on the market) and is what is embedded in pretty much every phone or device that does NFC. This chipset is very powerful, and can pretty much do it all, such as read and write to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
