# Fritzing sketch BN880_GPS_Schema (saved by Fritzing 0.9.4)

parts:
  Componente3 = Arduino Uno (Rev3)
  Componente2 = Adafruit MCP4725 Breakout Board - 12-Bit DAC [part_number="Adafruit #935"]

nets:
  N1: Componente3.D4, Componente2.RX
  N2: Componente3.D5_PWM, Componente2.TX
  5V: Componente3.5V, Componente2.VCC
  GND: Componente3.GND, Componente2.GND

custom parts:
  Adafruit MCP4725 Breakout Board - 12-Bit DAC: Your microcontroller probably has an ADC (analog -> digital converter) but does it have a DAC (digital -> analog converter)??? Now it can! This breakout board features the easy-to-use MCP4725 12-bit DAC. Control it via I2C and send it the value you want it to output, and the VOUT pin will have it. Great for audio / analog projects, such as when you can't use PWM but need a sine wave or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
