# Fritzing sketch MicroSD_Schema (saved by Fritzing 0.9.4)

parts:
  Componente1 = Adafruit MicroSD card breakout board [part_number="Adafruit #254"]
  Componente2 = Arduino Uno (Rev3)

nets:
  VCC: Componente1.VCC, Componente2.5V
  GND: Componente1.GND, Componente2.GND
  N1: Componente1.CLK, Componente2.D13/SCK
  N2: Componente1.DO, Componente2.D12/MISO
  N3: Componente1.DI, Componente2.D11_PWM/MOSI
  N4: Componente1.CS, Componente2.D10_PWM/SS

custom parts:
  Adafruit MicroSD card breakout board: Not just a simple breakout board, this microSD adapter goes the extra mile - designed for ease of use. Onboard 5v->3v regulator provides 150mA for power-hungry cards 3v level shifting means you can use this with ease on either 3v or 5v systems Uses a proper level shifting chip, not resistors: less problems, and faster read/write access Use 3 or 4 digital pins to read and write 2Gb+ of storage!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
