# Fritzing sketch Sharp_2Y0A21_Schema (saved by Fritzing 0.9.4)

parts:
  SHARP_2Y0A21 = Infrared Proximity Sensor
  Parte1 = Arduino Uno (Rev3)

nets:
  N1: SHARP_2Y0A21.Vout, Parte1.A0
  GND: SHARP_2Y0A21.GND, Parte1.GND
  VCC: SHARP_2Y0A21.Vcc, Parte1.5V
